// Logisim project Instruction Decoder.circ as structural Verilog: 1 circuit, main circuit Instruction Decoder
// Rd
module Instruction_Decoder (
  input  [31:0] Instruccion,
  output add,
  output addi,
  output blez,
  output pop,
  output out_6,
  output andi,
  output bgtz,
  output push,
  output mult,
  output ori,
  output bltz,
  output mulu,
  output xori,
  output lw,
  output halt,
  output div,
  output slti,
  output sw,
  output tty,
  output div_2,
  output sltiu,
  output j,
  output rnd,
  output div_3,
  output beq,
  output kbd,
  output \or ,
  output bne,
  output \nor ,
  output or_2,
  output slt,
  output [4:0] Rd,
  output [25:0] Constante,
  output sltu,
  output [4:0] Rt,
  output mfhi,
  output [4:0] Rs,
  output mflo,
  output nop,
  output [15:0] Constante_2,
  output jr
);

  wire _0, _53, _63, comparator_2_eq, comparator_3_eq, comparator_4_eq, comparator_5_eq, comparator_6_eq,
       comparator_7_eq, comparator_8_eq, comparator_9_eq, comparator_10_eq, comparator_11_eq,
       comparator_12_eq, comparator_13_eq, comparator_14_eq, comparator_15_eq, comparator_16_eq,
       comparator_17_eq, comparator_19_eq, comparator_20_eq, comparator_22_eq, comparator_23_eq,
       comparator_24_eq, comparator_25_eq;

  Comparator #(.width(6)) comparator_1 (.a(Instruccion[31:26]), .b({6{1'b0}}), .eq(_0));  // open: gt, lt
  and and_1 (add, _0, comparator_2_eq);
  Comparator #(.width(6)) comparator_2 (.a(Instruccion[5:0]), .b(6'b100000), .eq(comparator_2_eq));  // open: gt, lt
  and and_2 (out_6, _0, comparator_3_eq);
  Comparator #(.width(6)) comparator_3 (.a(Instruccion[5:0]), .b(6'b100010), .eq(comparator_3_eq));  // open: gt, lt
  and and_3 (mult, _0, comparator_4_eq);
  Comparator #(.width(6)) comparator_4 (.a(Instruccion[5:0]), .b(6'b011000), .eq(comparator_4_eq));  // open: gt, lt
  and and_4 (mulu, _0, comparator_5_eq);
  Comparator #(.width(6)) comparator_5 (.a(Instruccion[5:0]), .b(6'b011001), .eq(comparator_5_eq));  // open: gt, lt
  and and_5 (div, _0, comparator_6_eq);
  Comparator #(.width(6)) comparator_6 (.a(Instruccion[5:0]), .b(6'b011010), .eq(comparator_6_eq));  // open: gt, lt
  and and_6 (div_2, _0, comparator_7_eq);
  Comparator #(.width(6)) comparator_7 (.a(Instruccion[5:0]), .b(6'b011011), .eq(comparator_7_eq));  // open: gt, lt
  and and_7 (div_3, _0, comparator_8_eq);
  Comparator #(.width(6)) comparator_8 (.a(Instruccion[5:0]), .b(6'b100100), .eq(comparator_8_eq));  // open: gt, lt
  and and_8 (\or , _0, comparator_9_eq);
  Comparator #(.width(6)) comparator_9 (.a(Instruccion[5:0]), .b(6'b100101), .eq(comparator_9_eq));  // open: gt, lt
  Comparator #(.width(6)) comparator_10 (.a(Instruccion[5:0]), .b(6'b100111), .eq(comparator_10_eq));  // open: gt, lt
  Comparator #(.width(6)) comparator_11 (.a(Instruccion[5:0]), .b(6'b101000), .eq(comparator_11_eq));  // open: gt, lt
  Comparator #(.width(6)) comparator_12 (.a(Instruccion[5:0]), .b(6'b101010), .eq(comparator_12_eq));  // open: gt, lt
  Comparator #(.width(6)) comparator_13 (.a(Instruccion[5:0]), .b(6'b101011), .eq(comparator_13_eq));  // open: gt, lt
  Comparator #(.width(6)) comparator_14 (.a(Instruccion[5:0]), .b(6'b010000), .eq(comparator_14_eq));  // open: gt, lt
  Comparator #(.width(6)) comparator_15 (.a(Instruccion[5:0]), .b(6'b010010), .eq(comparator_15_eq));  // open: gt, lt
  Comparator #(.width(6)) comparator_16 (.a(Instruccion[5:0]), .b({6{1'b0}}), .eq(comparator_16_eq));  // open: gt, lt
  Comparator #(.width(6)) comparator_17 (.a(Instruccion[5:0]), .b(6'b001000), .eq(comparator_17_eq));  // open: gt, lt
  and and_9 (\nor , _0, comparator_10_eq);
  and and_10 (or_2, _0, comparator_11_eq);
  and and_11 (slt, _0, comparator_12_eq);
  and and_12 (sltu, _0, comparator_13_eq);
  and and_13 (mfhi, _0, comparator_14_eq);
  and and_14 (mflo, _0, comparator_15_eq);
  and and_15 (nop, _0, comparator_16_eq);
  and and_16 (jr, _0, comparator_17_eq);
  Comparator #(.width(6)) comparator_18 (.a(Instruccion[31:26]), .b(6'b111000), .eq(_53));  // open: gt, lt
  Comparator #(.width(6)) comparator_19 (.a(Instruccion[5:0]), .b({6{1'b0}}), .eq(comparator_19_eq));  // open: gt, lt
  Comparator #(.width(6)) comparator_20 (.a(Instruccion[5:0]), .b(6'b000001), .eq(comparator_20_eq));  // open: gt, lt
  Comparator #(.width(6)) comparator_21 (.a(Instruccion[31:26]), .b({6{1'b1}}), .eq(_63));  // open: gt, lt
  Comparator #(.width(6)) comparator_22 (.a(Instruccion[5:0]), .b({6{1'b1}}), .eq(comparator_22_eq));  // open: gt, lt
  Comparator #(.width(6)) comparator_23 (.a(Instruccion[5:0]), .b(6'b000001), .eq(comparator_23_eq));  // open: gt, lt
  Comparator #(.width(6)) comparator_24 (.a(Instruccion[5:0]), .b(6'b000010), .eq(comparator_24_eq));  // open: gt, lt
  Comparator #(.width(6)) comparator_25 (.a(Instruccion[5:0]), .b(6'b000100), .eq(comparator_25_eq));  // open: gt, lt
  and and_17 (pop, _53, comparator_19_eq);
  and and_18 (push, _53, comparator_20_eq);
  and and_19 (halt, _63, comparator_22_eq);
  and and_20 (tty, _63, comparator_23_eq);
  and and_21 (rnd, _63, comparator_24_eq);
  and and_22 (kbd, _63, comparator_25_eq);
  Comparator #(.width(6)) comparator_26 (.a(Instruccion[31:26]), .b(6'b001000), .eq(addi));  // open: gt, lt
  Comparator #(.width(6)) comparator_27 (.a(Instruccion[31:26]), .b(6'b001100), .eq(andi));  // open: gt, lt
  Comparator #(.width(6)) comparator_28 (.a(Instruccion[31:26]), .b(6'b001101), .eq(ori));  // open: gt, lt
  Comparator #(.width(6)) comparator_29 (.a(Instruccion[31:26]), .b(6'b001110), .eq(xori));  // open: gt, lt
  Comparator #(.width(6)) comparator_30 (.a(Instruccion[31:26]), .b(6'b001010), .eq(slti));  // open: gt, lt
  Comparator #(.width(6)) comparator_31 (.a(Instruccion[31:26]), .b(6'b001011), .eq(sltiu));  // open: gt, lt
  Comparator #(.width(6)) comparator_32 (.a(Instruccion[31:26]), .b(6'b000100), .eq(beq));  // open: gt, lt
  Comparator #(.width(6)) comparator_33 (.a(Instruccion[31:26]), .b(6'b000101), .eq(bne));  // open: gt, lt
  Comparator #(.width(6)) comparator_34 (.a(Instruccion[31:26]), .b(6'b000110), .eq(blez));  // open: gt, lt
  Comparator #(.width(6)) comparator_35 (.a(Instruccion[31:26]), .b(6'b000111), .eq(bgtz));  // open: gt, lt
  Comparator #(.width(6)) comparator_36 (.a(Instruccion[31:26]), .b(6'b000001), .eq(bltz));  // open: gt, lt
  Comparator #(.width(6)) comparator_37 (.a(Instruccion[31:26]), .b(6'b100011), .eq(lw));  // open: gt, lt
  Comparator #(.width(6)) comparator_38 (.a(Instruccion[31:26]), .b(6'b101011), .eq(sw));  // open: gt, lt
  Comparator #(.width(6)) comparator_39 (.a(Instruccion[31:26]), .b(6'b000010), .eq(j));  // open: gt, lt

  assign Constante = Instruccion[25:0];
  assign Constante_2 = Instruccion[15:0];
  assign Rd = Instruccion[15:11];
  assign Rs = Instruccion[25:21];
  assign Rt = Instruccion[20:16];

  // Other names for the same wires on the sheet: and = div_3; Constante_t[15:0] = Instruccion[15:0];
  //   Destino[25:0] = Instruccion[25:0]; Function_Code[5:0] = Instruccion[5:0]; X[4:0] = Instruccion[10:6];
  //   divu = div_2; Operation_Code[5:0] = Instruccion[31:26]; sub = out_6; xor = or_2

  // Notes on the sheet:
  //   10 0000
  //   10 0010
  //   01 1000 
  //   01 1001
  //   01 1010 
  //    01 1011
  //   10 0100
  //    10 0101
  //   Tipo R 000000
  //    10 0111
  //    10 1000
  //   10 1010
  //   10 1011
  //   01 0000 
  //   01 0010
  //   00 0000
  //   00 1000 
  //   Tipo R 11 1000 
  //   11 1000
  //   00 0000
  //   00 0001
  //   Tipo R 11 1111
  //   11 1111
  //   11 1111
  //   00 0001
  //   00 0010
  //   00 0100
  //   Tipo I
  //   00 1000 
  //   00 1100
  //    00 1101
  //    00 1110
  //   00 1010 
  //   00 1011
  //   00 0100
  //   00 0101
  //   00 0110
  //   00 0111
  //   00 0001
  //   10 0011
  //   10 1011
  //   00 0010 
endmodule
