// Logisim project save.circ as structural Verilog: 7 circuits, main circuit ALU
module ALU (
  input  Sign,
  input  [3:0] Selector,
  input  [31:0] A,
  input  [31:0] B,
  output [31:0] Output,
  output [31:0] Lo,
  output [31:0] Hi,
  output Hi_Lo
);

  wire and_2_out, mul;
  wire [31:0] add, \and , div_hi, div_lo, mul_hi, mul_lo, \nor , \or , slt, sub, \xor ;

  and and_1 (mul, ~Selector[0], ~Selector[1], Selector[2], ~Selector[3]);  // AND_Gate
  and and_2 (and_2_out, ~Selector[0], ~Selector[1], ~Selector[2], Selector[3]);  // AND_Gate
  or or_1 (Hi_Lo, mul, and_2_out);
  Adder #(.width(32)) adder_1 (.a(A), .b(B), .out(add));  // open: cin, cout
  Subtractor #(.width(32)) subtractor_1 (.a(A), .b(B), .out(sub));  // open: bin, bout
  Multiplier multiplier_1 (.A(A), .B(B), .Signed(Sign), .Lo(mul_lo), .Hi(mul_hi));  // open: Cin
  Divider divider_1 (.A(A), .B(B), .Signed(Sign), .Lo(div_lo), .Hi(div_hi));
  Comparator comparator_1 (.Sign(Sign), .Output(slt), .A(A), .B(B));
  assign \and  = A & B;  // AND_Gate and_3, 32 bits wide
  assign \or  = A | B;  // OR_Gate or_2, 32 bits wide
  assign \nor  = ~(A | B);  // NOR_Gate nor_1, 32 bits wide
  assign \xor  = A ^ B;  // XOR_Gate xor_1, 32 bits wide
  Multiplexer #(.select(4), .width(32), .enable("false")) multiplexer_1 (
    .in0(slt), .in1(\and ), .in2(sub), .in3(\or ), .in5(\nor ), .in9(\xor ), .in14(add), .out(Output),
    .sel(Selector));  // open: in4, in6, in7, in8, in10, in11, in12, in13, in15
  Multiplexer #(.width(32), .enable("false")) multiplexer_2 (.in0(div_lo), .in1(mul_lo), .out(Lo), .sel(mul));
  Multiplexer #(.width(32), .enable("false")) multiplexer_3 (.in0(div_hi), .in1(mul_hi), .out(Hi), .sel(mul));

  // Other names for the same wires on the sheet: select[3:0] = Selector; sn = Sign
endmodule

// Less
module Comparator (
  input  [31:0] A,
  input  [31:0] B,
  input  Sign,
  output [31:0] Output
);

  wire and_1_out, and_2_out, comparator_1_lt, comparator_2_lt, or_1_out;

  Comparator_part #(.width(32)) comparator_1 (.a(A), .b(B), .lt(comparator_1_lt));  // open: gt, eq
  Comparator_part #(.width(32), .mode("unsigned")) comparator_2 (.a(A), .b(B), .lt(comparator_2_lt));  // open: gt, eq
  and and_1 (and_1_out, comparator_1_lt, Sign);
  and and_2 (and_2_out, ~Sign, comparator_2_lt);  // AND_Gate
  or or_1 (or_1_out, and_1_out, and_2_out);
  assign Output = {{31{1'b0}}, or_1_out};  // Bit_Extender bit_extender_1
endmodule

module ALU_Encoder (
  input  add,
  input  sub,
  input  mul,
  input  umul,
  input  div,
  input  udiv,
  input  slt,
  input  uslt,
  input  \and ,
  input  \or ,
  input  \nor ,
  input  \xor ,
  input  addi,
  input  slti,
  input  uslti,
  input  andi,
  input  ori,
  input  xori,
  output Input,
  output Sign,
  output [3:0] Selector
);

  wire Add_t, And_t, Div_t, Mul_t, Or_t, Xor_t;

  or or_1 (Add_t, add, addi);
  or or_2 (Mul_t, mul, umul);
  or or_3 (Div_t, div, udiv);
  or or_4 (Selector[0], \nor , And_t, Or_t, Xor_t);
  or or_5 (Selector[1], sub, Add_t, Or_t);
  or or_6 (And_t, \and , andi);
  or or_7 (Or_t, \or , ori);
  or or_8 (Xor_t, \xor , xori);
  or or_9 (Selector[2], \nor , Add_t, Mul_t);
  or or_10 (Selector[3], Xor_t, Add_t, Div_t);
  or or_11 (Input, addi, slti, uslti, andi, ori, xori);
  or or_12 (Sign, mul, div, slt, slti);

  // Other names for the same wires on the sheet: b0 = Selector[0]; b1 = Selector[1]; b2 = Selector[2];
  //   b3 = Selector[3]
endmodule

// Mult
module Multiplier (
  input  [31:0] A,
  input  [31:0] B,
  input  [31:0] Cin,
  input  Signed,
  output [31:0] Lo,
  output [31:0] Hi
);

  wire snAB;
  wire [31:0] adder_1_out, multiplexer_1_out, multiplexer_2_out, multiplier_2_cout, shi, slo, uhi, ulo;

  // Probe on A
  // Probe on B
  Multiplexer #(.width(32), .enable("false")) multiplexer_1 (
    .in0({32{1'b0}}), .in1(B), .out(multiplexer_1_out), .sel(A[31]));
  Multiplexer #(.width(32), .enable("false")) multiplexer_2 (
    .in0({32{1'b0}}), .in1(A), .out(multiplexer_2_out), .sel(B[31]));
  Multiplexer #(.width(32), .enable("false")) multiplexer_3 (.in0(ulo), .in1(slo), .out(Lo), .sel(Signed));
  Multiplexer #(.width(32), .enable("false")) multiplexer_4 (.in0(uhi), .in1(shi), .out(Hi), .sel(Signed));
  Multiplier_part #(.width(32)) multiplier_1 (.a(A), .b(B), .out(slo), .cin(Cin), .cout(shi));
  Multiplier_part #(.width(32)) multiplier_2 (.a(A), .b(B), .out(ulo), .cin(Cin), .cout(multiplier_2_cout));
  Adder #(.width(32)) adder_1 (.a(multiplexer_1_out), .b(multiplexer_2_out), .out(adder_1_out));  // open: cin, cout
  Adder #(.width(32)) adder_2 (.a(multiplier_2_cout), .b(adder_1_out), .out(uhi));  // open: cin, cout
  xor xor_1 (snAB, A[31], B[31]);

  // Other names for the same wires on the sheet: snA = A[31]; snB = B[31]; sn = Signed
endmodule

// Div
module Divider (
  input  [31:0] A,
  input  [31:0] B,
  input  Signed,
  output [31:0] Lo,
  output [31:0] Hi
);

  wire snAB;
  wire [31:0] divider_2_out, multiplexer_1_out, multiplexer_2_out, negator_1_out, negator_2_out,
       negator_3_out, shi, slo, uhi, ulo;

  Divider_part #(.width(32)) divider_1 (.a(A), .b(B), .out(ulo), .rem(uhi));  // open: upper
  Multiplexer #(.width(32), .enable("false")) multiplexer_1 (
    .in0(A), .in1(negator_1_out), .out(multiplexer_1_out), .sel(A[31]));
  Negator #(.width(32)) negator_1 (.in(A), .out(negator_1_out));
  Multiplexer #(.width(32), .enable("false")) multiplexer_2 (
    .in0(B), .in1(negator_2_out), .out(multiplexer_2_out), .sel(B[31]));
  Negator #(.width(32)) negator_2 (.in(B), .out(negator_2_out));
  Multiplexer #(.width(32), .enable("false")) multiplexer_3 (.in0(ulo), .in1(slo), .out(Lo), .sel(Signed));
  Multiplexer #(.width(32), .enable("false")) multiplexer_4 (.in0(uhi), .in1(shi), .out(Hi), .sel(Signed));
  Divider_part #(.width(32)) divider_2 (
    .a(multiplexer_1_out), .b(multiplexer_2_out), .out(divider_2_out), .rem(shi));  // open: upper
  Negator #(.width(32)) negator_3 (.in(divider_2_out), .out(negator_3_out));
  Multiplexer #(.width(32), .enable("false")) multiplexer_5 (
    .in0(divider_2_out), .in1(negator_3_out), .out(slo), .sel(snAB));
  xor xor_1 (snAB, A[31], B[31]);

  // Other names for the same wires on the sheet: snA = A[31]; snB = B[31]; sn = Signed
endmodule

module Register_File_In (
  input  Lw,
  input  [31:0] ALU,
  input  Pop,
  input  Mflo,
  input  Mfhi,
  input  Kbd,
  input  [31:0] Rand,
  input  Rand_2,
  input  [31:0] Mem,
  input  [31:0] Lo,
  input  [31:0] Hi,
  input  [6:0] Kbd_2,
  output [31:0] Output
);

  wire [2:0] select;

  or or_1 (select[2], Lw, Kbd, Rand_2);
  or or_2 (select[1], Pop, Mflo, Kbd);
  or or_3 (select[0], Pop, Mfhi, Rand_2);
  Multiplexer #(.select(3), .width(32), .enable("false")) multiplexer_1 (
    .in0(ALU), .in1(Hi), .in2(Lo), .in3(Mem), .in4(Mem), .in5(Rand), .in6({{25{1'b0}}, Kbd_2}), .out(Output),
    .sel(select));  // open: in7

  // Other names for the same wires on the sheet: kbdin[6:0] = Kbd_2; rand_t = Rand_2; randin[31:0] = Rand
endmodule

module Register_File (
  input  Clock,
  input  Reset,
  input  RW,
  input  Push,
  input  Pop,
  input  [4:0] SA,
  input  [4:0] SB,
  input  [4:0] DA,
  input  [31:0] DI,
  input  [31:0] Hi,
  input  [31:0] Lo,
  input  Hi_Lo,
  input  enPC,
  output [31:0] A,
  output [31:0] B,
  output [31:0] Hi_2,
  output [31:0] Lo_2,
  output [31:0] SP
);

  wire and_1_out, L0, L1, L2, L3, L4, L5, L6, L7, L8, L9, L10, L11, L12, L13, L14, L15, L16, L17, L18, L19,
       L20, L21, L22, L23, L24, L25, L26, L27, L28, L29, L30, L31, LSP, or_1_out;
  wire [31:0] adder_1_out, multiplexer_2_out, multiplexer_4_out, Q0, Q1, Q2, Q3, Q4, Q5, Q6, Q7, Q8, Q9, Q10,
       Q11, Q12, Q13, Q14, Q15, Q16, Q17, Q18, Q19, Q20, Q21, Q22, Q23, Q24, Q25, Q26, Q27, Q28, Q29, Q30,
       SP_t, subtractor_1_out;

  Register #(.width(32)) register_1 (.D({32{1'b0}}), .en(L0), .Q(Q0), .clk(Clock), .clr(Reset));
  Register #(.width(32)) register_2 (.D(DI), .en(L1), .Q(Q1), .clk(Clock), .clr(Reset));
  Register #(.width(32)) register_3 (.D(DI), .en(L2), .Q(Q2), .clk(Clock), .clr(Reset));
  Register #(.width(32)) register_4 (.D(DI), .en(L3), .Q(Q3), .clk(Clock), .clr(Reset));
  Register #(.width(32)) register_5 (.D(Hi), .en(Hi_Lo), .Q(Hi_2), .clk(Clock));  // open: clr
  Register #(.width(32)) register_6 (.D(Lo), .en(Hi_Lo), .Q(Lo_2), .clk(Clock));  // open: clr
  Register #(.width(32)) register_7 (.D(DI), .en(L4), .Q(Q4), .clk(Clock), .clr(Reset));
  Register #(.width(32)) register_8 (.D(DI), .en(L5), .Q(Q5), .clk(Clock), .clr(Reset));
  Register #(.width(32)) register_9 (.D(DI), .en(L6), .Q(Q6), .clk(Clock), .clr(Reset));
  Register #(.width(32)) register_10 (.D(DI), .en(L7), .Q(Q7), .clk(Clock), .clr(Reset));
  Register #(.width(32)) register_11 (.D(DI), .en(L8), .Q(Q8), .clk(Clock), .clr(Reset));
  Register #(.width(32)) register_12 (.D(DI), .en(L9), .Q(Q9), .clk(Clock), .clr(Reset));
  Register #(.width(32)) register_13 (.D(DI), .en(L10), .Q(Q10), .clk(Clock), .clr(Reset));
  Register #(.width(32)) register_14 (.D(DI), .en(L11), .Q(Q11), .clk(Clock), .clr(Reset));
  Multiplexer #(.select(5), .width(32), .enable("false")) multiplexer_1 (
    .in0(Q0), .in1(Q1), .in2(Q2), .in3(Q3), .in4(Q4), .in5(Q5), .in6(Q6), .in7(Q7), .in8(Q8), .in9(Q9),
    .in10(Q10), .in11(Q11), .in12(Q12), .in13(Q13), .in14(Q14), .in15(Q15), .in16(Q16), .in17(Q17),
    .in18(Q18), .in19(Q19), .in20(Q20), .in21(Q21), .in22(Q22), .in23(Q23), .in24(Q24), .in25(Q25),
    .in26(Q26), .in27(Q27), .in28(Q28), .in29(Q29), .in30(Q30), .in31(SP), .out(A), .sel(SA));
  Subtractor #(.width(32)) subtractor_1 (.a(SP), .b(32'h4), .out(subtractor_1_out));  // open: bin, bout
  Adder #(.width(32)) adder_1 (.a(32'h4), .b(SP), .out(adder_1_out));  // open: cin, cout
  Register #(.width(32)) register_15 (.D(DI), .en(L12), .Q(Q12), .clk(Clock), .clr(Reset));
  Register #(.width(32)) register_16 (.D(DI), .en(L13), .Q(Q13), .clk(Clock), .clr(Reset));
  Register #(.width(32)) register_17 (.D(DI), .en(L14), .Q(Q14), .clk(Clock), .clr(Reset));
  Register #(.width(32)) register_18 (.D(DI), .en(L15), .Q(Q15), .clk(Clock), .clr(Reset));
  Multiplexer #(.width(32), .enable("false")) multiplexer_2 (
    .in0(subtractor_1_out), .in1(adder_1_out), .out(multiplexer_2_out), .sel(Pop));
  Register #(.width(32)) register_19 (.D(DI), .en(L16), .Q(Q16), .clk(Clock), .clr(Reset));
  Register #(.width(32)) register_20 (.D(DI), .en(L17), .Q(Q17), .clk(Clock), .clr(Reset));
  Register #(.width(32)) register_21 (.D(DI), .en(L18), .Q(Q18), .clk(Clock), .clr(Reset));
  Register #(.width(32)) register_22 (.D(DI), .en(L19), .Q(Q19), .clk(Clock), .clr(Reset));
  Multiplexer #(.select(5), .width(32), .enable("false")) multiplexer_3 (
    .in0(Q0), .in1(Q1), .in2(Q2), .in3(Q3), .in4(Q4), .in5(Q5), .in6(Q6), .in7(Q7), .in8(Q8), .in9(Q9),
    .in10(Q10), .in11(Q11), .in12(Q12), .in13(Q13), .in14(Q14), .in15(Q15), .in16(Q16), .in17(Q17),
    .in18(Q18), .in19(Q19), .in20(Q20), .in21(Q21), .in22(Q22), .in23(Q23), .in24(Q24), .in25(Q25),
    .in26(Q26), .in27(Q27), .in28(Q28), .in29(Q29), .in30(Q30), .in31(SP), .out(B), .sel(SB));
  Multiplexer #(.width(32), .enable("false")) multiplexer_4 (
    .in0(multiplexer_2_out), .in1({32{1'b1}}), .out(multiplexer_4_out), .sel(Reset));
  Register #(.width(32)) register_23 (.D(DI), .en(L20), .Q(Q20), .clk(Clock), .clr(Reset));
  Register #(.width(32)) register_24 (.D(DI), .en(L21), .Q(Q21), .clk(Clock), .clr(Reset));
  Register #(.width(32)) register_25 (.D(DI), .en(L22), .Q(Q22), .clk(Clock), .clr(Reset));
  Register #(.width(32)) register_26 (.D(DI), .en(L23), .Q(Q23), .clk(Clock), .clr(Reset));
  Multiplexer #(.width(32), .enable("false")) multiplexer_5 (.in0(multiplexer_4_out), .in1(DI), .out(SP_t), .sel(L31));
  Demultiplexer #(.select(5), .enable("false")) demultiplexer_1 (
    .out0(L0), .out1(L1), .out2(L2), .out3(L3), .out4(L4), .out5(L5), .out6(L6), .out7(L7), .out8(L8),
    .out9(L9), .out10(L10), .out11(L11), .out12(L12), .out13(L13), .out14(L14), .out15(L15), .out16(L16),
    .out17(L17), .out18(L18), .out19(L19), .out20(L20), .out21(L21), .out22(L22), .out23(L23), .out24(L24),
    .out25(L25), .out26(L26), .out27(L27), .out28(L28), .out29(L29), .out30(L30), .out31(L31), .in(RW),
    .sel(DA));
  and and_1 (and_1_out, enPC, or_1_out);
  or or_1 (or_1_out, Push, Pop);
  Register #(.width(32)) register_27 (.D(DI), .en(L24), .Q(Q24), .clk(Clock), .clr(Reset));
  Register #(.width(32)) register_28 (.D(DI), .en(L25), .Q(Q25), .clk(Clock), .clr(Reset));
  Register #(.width(32)) register_29 (.D(DI), .en(L26), .Q(Q26), .clk(Clock), .clr(Reset));
  Register #(.width(32)) register_30 (.D(DI), .en(L27), .Q(Q27), .clk(Clock), .clr(Reset));
  Register #(.width(32)) register_31 (.D(DI), .en(L28), .Q(Q28), .clk(Clock), .clr(Reset));
  Register #(.width(32)) register_32 (.D(DI), .en(L29), .Q(Q29), .clk(Clock), .clr(Reset));
  Register #(.width(32)) register_33 (.D(DI), .en(L30), .Q(Q30), .clk(Clock), .clr(Reset));
  Register #(.width(32)) register_34 (.D(SP_t), .en(LSP), .Q(SP), .clk(Clock));  // open: clr
  or or_2 (LSP, and_1_out, L31, Reset);

  // Other names for the same wires on the sheet: CLK = Clock; Q31[31:0] = SP; RS = Reset
endmodule
